// Logisim project shr.circ as structural Verilog
module shr (
  input  [7:0] In_A,
  input  [2:0] In_B,
  output [7:0] R
);

  wire [7:0] multiplexer_1_out, multiplexer_2_out, shift_right1_1_out_2, shift_right2_1_out_2,
       shift_right4_1_out_2;

  Multiplexer #(.width(8), .enable("false")) multiplexer_1 (
    .in0(In_A), .in1(shift_right1_1_out_2), .out(multiplexer_1_out), .sel(In_B[0]));
  shift_right1 shift_right1_1 (.out_2(shift_right1_1_out_2), .in_1(In_A));
  shift_right2 shift_right2_1 (.out_2(shift_right2_1_out_2), .in_1(multiplexer_1_out));
  Multiplexer #(.width(8), .enable("false")) multiplexer_2 (
    .in0(multiplexer_1_out), .in1(shift_right2_1_out_2), .out(multiplexer_2_out), .sel(In_B[1]));
  Multiplexer #(.width(8), .enable("false")) multiplexer_3 (
    .in0(multiplexer_2_out), .in1(shift_right4_1_out_2), .out(R), .sel(In_B[2]));
  shift_right4 shift_right4_1 (.out_2(shift_right4_1_out_2), .in_1(multiplexer_2_out));

  // Other names for the same wires on the sheet: A[7:0] = In_A; B[2:0] = In_B; Result[7:0] = R

  // Notes on the sheet:
  //   ------------------------- Put your circuit below this line ------------------
endmodule

module shift_right1 (
  input  [7:0] in_1,
  output [7:0] out_2
);


  assign out_2 = {1'b0, in_1[7:1]};

  // Other names for the same wires on the sheet: A[7:0] = in_1
endmodule

module shift_right2 (
  input  [7:0] in_1,
  output [7:0] out_2
);


  assign out_2 = {2'b00, in_1[7:2]};

  // Other names for the same wires on the sheet: A[7:0] = in_1
endmodule

module shift_right4 (
  input  [7:0] in_1,
  output [7:0] out_2
);


  assign out_2 = {4'b0000, in_1[7:4]};

  // Other names for the same wires on the sheet: A[7:0] = in_1
endmodule
